# Fritzing sketch NNF (saved by Fritzing 0.9.3b)
breadboards: 2

parts:
  CPM = WeMos D1 Mini
  MTHM = WeMos D1 Mini
  WPM = WeMos D1 Mini
  S1 = H-Bridge with L298N
  WATER_PUMP1 = water pump/motor  # not connected
  JACK1 = 2.1mm Barrel Jack with Terminal Block
  DFRobot_DFPlayer_Mini1 = DFRobot DFPlayer Mini [part_number=DFR0299]
  PIR1 = PIR sensor
  R1 = Resistor [tolerance=±5% resistance=1k package=THT]
  R2 = Resistor [tolerance=±5% resistance=1k package=THT]
  SP1 = SPEAKER [package=pcb_mount_speaker]
  부품1 = FC-28 Soil Hygrometer Module
  부품2 = FC-28 Soil Hygrometer Module - Probe
  DHT1 = DHT11 Humitidy and Temperature Sensor
  R3 = Resistor [tolerance=±5% resistance=5.1k package=THT]
  JACK2 = 2.1mm Barrel Jack with Terminal Block
  JACK3 = 2.1mm Barrel Jack with Terminal Block
  JACK4 = 2.1mm Barrel Jack with Terminal Block

nets:
  5V: CPM.5V, DFRobot_DFPlayer_Mini1.VCC, PIR1.VDD, JACK3.POS
  N1: CPM.D1, PIR1.SIG
  N2: CPM.G, DFRobot_DFPlayer_Mini1.GND-1, DFRobot_DFPlayer_Mini1.GND-2, PIR1.GND, JACK3.NEG
  N3: CPM.RX, R2.Pin_0
  N4: CPM.TX, R1.Pin_0
  5V_2: MTHM.5V, 부품1.VCC, DHT1.VDD, R3.Pin_1, JACK4.POS
  N5: MTHM.A0, 부품1.AO
  N6: MTHM.D4, DHT1.DATA, R3.Pin_0
  GND: MTHM.G, 부품1.GND, DHT1.GND, JACK4.NEG
  N7: WPM.5V, JACK2.POS
  N8: WPM.D7, S1.IN1
  N9: WPM.D8, S1.IN2
  N10: WPM.G, JACK2.NEG
  N11: S1.12V, JACK1.POS
  N12: S1.GND, JACK1.NEG
  N13: DFRobot_DFPlayer_Mini1.RX, R1.Pin_1
  N14: DFRobot_DFPlayer_Mini1.TX, R2.Pin_1
  N15: DFRobot_DFPlayer_Mini1.SPK_1, SP1.-
  N16: DFRobot_DFPlayer_Mini1.SPK_2, SP1.+
  N17: 부품1.POS, 부품2.POS
  N18: 부품1.NEG, 부품2.NEG

custom parts:
  H-Bridge with L298N: h-bridge
  water pump/motor: WATER PUMP BY ARDUBLOCKTR
  FC-28 Soil Hygrometer Module: The FC-28 is a soil hygrometer module that uses the Texas Instruments LM393 comparator chip to provide an analog measurement of soil humidity. The digital output is high when soil moisture is over a certain threshold, as determined by adjusting the potentiometer.
  FC-28 Soil Hygrometer Module - Probe: The FC-28 is a soil hygrometer module that uses the Texas Instruments LM393 comparator chip to provide an analog measurement of soil humidity.
  DHT11 Humitidy and Temperature Sensor: DHT11 Humidity and Temperature Sensor
